# Fritzing sketch Tilt_3and4pin (saved by Fritzing 0.9.3b)
breadboards: 2

parts:
  Part1 = Arduino Uno (Rev3)
  Mod1 = KY-017 Mercury Tilt Switch [package="Breakout board"]
  Part2 = Arduino Uno (Rev3)
  Mod3 = KY-027 Magic Light Cup Module [package="Breakout board"]

nets:
  GND: Part1.GND, Mod1.Vin
  N1: Part1.D3_PWM, Mod1.S
  N2: Part1.5V, Mod1.-
  N3: Part2.D8, Mod3.S
  N4: Part2.D9_PWM, Mod3.L
  N5: Part2.5V, Mod3.+
  N6: Part2.GND, Mod3.G

custom parts:
  KY-017 Mercury Tilt Switch: KY-017 mercury tilt switch module, it uses a small mercury ball that completes the circuit when you tilt the module.
  KY-027 Magic Light Cup Module: KY-0127 Magic Light Cup module is a set of two boards, each one has a led and a mercury tilt switch. Using PWM to drive the LEDs on each module you can achieve the effect of light being "magically" transferred from one module to the other when tilting them.
